# Fritzing sketch rocket (saved by Fritzing 0.9.6b)
breadboards: 1

parts:
  M1 = RioRand LM2596
  Part1 = Arduino Nano (Rev3.0)
  Mod1 = ossoyoo-lora-module
  BAT1 = Battery Holders [package=lipo-1100mAh]
  Q1 = Basic FET N-Channel [package="DPak [SMD]"]
  LED1 = LED - 3mm [color="Red (633nm)" current=0.030 package="3 mm [THT]"]
  R1 = Resistor [tolerance=±5% power=0.25 resistance=220 package=THT]
  R2 = Resistor [tolerance=±5% resistance=10k package="2010 [SMD]"]

nets:
  N1: M1.Pin_1, BAT1.+
  N2: M1.Pin_2, BAT1.-
  N3: M1.Pin_3, Part1.VIN, R1.Pin_1
  GND: M1.Pin_4, Part1.GND, Mod1.M0, Mod1.M1, Mod1.GND, Q1.source
  N4: Part1.D1/TX, Mod1.TXD
  N5: Part1.D0/RX, Mod1.RXD
  N6: Part1.D3, Q1.Gate, R2.Pin_0
  N7: Q1.drain, LED1.cathode, R2.Pin_1
  N8: LED1.anode, R1.Pin_0

custom parts:
  ossoyoo-lora-module: Osoyoo Long Distance wireless transceiver Uart LoRa Module.
